// Logisim project 2 bit Combinational multiplier.circ as structural Verilog: 1 circuit, main circuit main
module main (
  input  B1,
  input  B0,
  input  A1,
  input  A0,
  output M3,
  output M2,
  output M1,
  output M0
);

  wire and_1_out, and_2_out, and_3_out, HA2_c;

  and and_1 (and_1_out, B1, A1);
  and and_2 (and_2_out, B1, A0);
  Half_Adder_main HA1 (.A(HA2_c), .in_2(and_1_out), .S(M2), .C(M3));
  and and_3 (and_3_out, B0, A1);
  Half_Adder_main HA2 (.A(and_3_out), .in_2(and_2_out), .S(M1), .C(HA2_c));
  and and_4 (M0, B0, A0);
endmodule
