// Logisim project 2 bit full subtractor.circ as structural Verilog: 1 circuit, main circuit main
module main (
  input  A1,
  input  B1,
  input  A0,
  input  B0,
  input  Bin,
  output Bout,
  output D0,
  output D1
);

  wire main_1_bout;

  Full_Subtractor_using_half_subtractor_main main_1 (.A(B0), .B(A0), .Bin(Bin), .D(D0), .Bout(main_1_bout));
  Full_Subtractor_using_half_subtractor_main main_2 (.A(B1), .B(A1), .Bin(main_1_bout), .D(D1), .Bout(Bout));
endmodule
