// Logisim project 2X4 Decoder.circ as structural Verilog: 1 circuit, main circuit main
module main (
  input  B,
  input  E,
  input  A,
  output A0,
  output A1,
  output A2,
  output A3
);

  wire NOT1_out, NOT2_out, NOT3_out;

  not NOT1 (NOT1_out, A);
  not NOT2 (NOT2_out, B);
  not NOT3 (NOT3_out, E);
  and AND1 (A0, NOT1_out, NOT2_out, NOT3_out);
  and AND2 (A1, A, NOT2_out, NOT3_out);
  and AND3 (A2, NOT1_out, B, NOT3_out);
  and AND4 (A3, A, B, NOT3_out);
endmodule
