// Logisim project 4 Bit Full Subtractor.circ as structural Verilog: 1 circuit, main circuit main
module main (
  input  B0,
  input  A0,
  input  B1,
  input  A1,
  input  B2,
  input  A2,
  input  B3,
  input  A3,
  input  Bin,
  output Bout,
  output D0,
  output D1,
  output D2,
  output D3
);

  wire FS0_bout, FS1_bout, FS2_bout;

  Full_Subtractor_using_half_subtractor_main FS0 (.A(A0), .B(B0), .Bin(Bin), .D(D0), .Bout(FS0_bout));
  Full_Subtractor_using_half_subtractor_main FS1 (.A(A1), .B(B1), .Bin(FS0_bout), .D(D1), .Bout(FS1_bout));
  Full_Subtractor_using_half_subtractor_main FS2 (.A(A2), .B(B2), .Bin(FS1_bout), .D(D2), .Bout(FS2_bout));
  Full_Subtractor_using_half_subtractor_main FS3 (.A(A3), .B(B3), .Bin(FS2_bout), .D(D3), .Bout(Bout));
endmodule
