// Logisim project 4 Bit Subtractor And Adder.circ as structural Verilog: 1 circuit, main circuit main
module main (
  input  B0,
  input  B1,
  input  B2,
  input  B3,
  input  A0,
  input  A1,
  input  A2,
  input  A3,
  input  Cin,
  output Cout,
  output S0,
  output S1,
  output S2,
  output S3
);

  wire FA0_c, FA1_c, FA2_c, xor_1_out, xor_2_out, xor_3_out, xor_4_out;

  xor xor_1 (xor_1_out, Cin, B0);
  Full_Adder_using_half_adder_main FA0 (.A(A0), .B(xor_1_out), .Cin(Cin), .S(S0), .C(FA0_c));
  xor xor_2 (xor_2_out, Cin, B1);
  Full_Adder_using_half_adder_main FA1 (.A(A1), .B(xor_2_out), .Cin(FA0_c), .S(S1), .C(FA1_c));
  xor xor_3 (xor_3_out, Cin, B2);
  Full_Adder_using_half_adder_main FA2 (.A(A2), .B(xor_3_out), .Cin(FA1_c), .S(S2), .C(FA2_c));
  xor xor_4 (xor_4_out, Cin, B3);
  Full_Adder_using_half_adder_main FA3 (.A(A3), .B(xor_4_out), .Cin(FA2_c), .S(S3), .C(Cout));
endmodule
