// Logisim project 4 bit combinational multiplier.circ as structural Verilog: 1 circuit, main circuit main
module main (
  input  B3,
  input  B2,
  input  B1,
  input  B0,
  input  A3,
  input  A2,
  input  A1,
  input  A0,
  output M5,
  output M3,
  output M2,
  output M2_2,
  output M1,
  output M0,
  output M4
);

  wire AND3_out, AND4_out, AND5_out, AND6_out, AND8_out, AND9_out, AND10_out, AND11_out, AND12_out,
       AND13_out, AND14_out, AND15_out, AND16_out, HA0_p3, HA1_p4, main_1_p1, main_1_p3, main_2_p1,
       main_2_p5, main_3_p1, main_3_p3, main_4_p1, main_4_p5, main_5_p1, main_5_p5, main_6_p3, main_7_p3,
       main_7_p4, main_7_p5, main_8_p4, main_9_p1, main_10_p1;

  and AND16 (AND16_out, B3, A3);
  // Full_Adder_main main_1: pin names not known; wires that end beside it: main_1_p1, M5, main_1_p3, AND16_out, M4
  and AND14 (AND14_out, B2, A3);
  and AND15 (AND15_out, B3, A2);
  // Full_Adder_main main_2: pin names not known; wires that end beside it: main_2_p1, main_1_p1, AND15_out, AND14_out, main_2_p5
  // Full_Adder_main main_3: pin names not known; wires that end beside it: main_3_p1, main_1_p3, main_3_p3, main_2_p5
  and AND12 (AND12_out, B2, A2);
  and AND13 (AND13_out, B3, A1);
  and AND11 (AND11_out, B1, A3);
  // Full_Adder_main main_4: pin names not known; wires that end beside it: main_4_p1, main_2_p1, AND12_out, AND11_out, main_4_p5
  // Full_Adder_main main_5: pin names not known; wires that end beside it: main_5_p1, main_3_p1, AND13_out, main_4_p5, main_5_p5
  // Half_Adder_main main_6: pin names not known; wires that end beside it: main_5_p5, main_3_p3, main_6_p3, M3
  and AND9 (AND9_out, B2, A1);
  and AND10 (AND10_out, B3, A0);
  and AND8 (AND8_out, B1, A2);
  // Half_Adder_main main_7: pin names not known; wires that end beside it: AND8_out, main_4_p1, main_7_p3, main_7_p4, main_7_p5
  and AND6 (AND6_out, B2, A0);
  and AND7 (main_7_p3, B0, A3);
  // Full_Adder_main main_8: pin names not known; wires that end beside it: main_5_p1, AND9_out, main_7_p4, main_8_p4
  // Full_Adder_main main_9: pin names not known; wires that end beside it: main_9_p1, main_6_p3, AND10_out, main_8_p4, M2
  and AND4 (AND4_out, B0, A2);
  and AND5 (AND5_out, B1, A1);
  // Half_Adder_main HA1: pin names not known; wires that end beside it: AND5_out, main_7_p5, AND4_out, HA1_p4
  // Full_Adder_main main_10: pin names not known; wires that end beside it: main_10_p1, main_9_p1, AND6_out, HA1_p4, M2_2
  and AND3 (AND3_out, B1, A0);
  // Half_Adder_main HA0: pin names not known; wires that end beside it: AND3_out, main_10_p1, HA0_p3, M1
  and _2 (HA0_p3, B0, A1);
  and AND1 (M0, B0, A0);
endmodule
