// Logisim project 4-bit synchronous  DOWN counter.circ as structural Verilog: 1 circuit, main circuit main
module main (
  input  Enable,
  input  Preset,
  input  Reset,
  output Q0,
  output Q1,
  output Q2,
  output Q3
);

  wire AND_2_out, AND_out, Clock_out, JK0_qn, JK1_qn, JK2_qn;

  Clock Clock (.out(Clock_out));
  J_K_Flip_Flop JK0 (
    .J(1'b1), .clk(Clock_out), .K(1'b1), .Q(Q0), .Qn(JK0_qn), .preset(Preset), .en(Enable), .reset(Reset));
  J_K_Flip_Flop JK1 (
    .J(JK0_qn), .clk(Clock_out), .K(JK0_qn), .Q(Q1), .Qn(JK1_qn), .preset(Preset), .en(Enable), .reset(Reset));
  and AND (AND_out, JK1_qn, JK0_qn);
  J_K_Flip_Flop JK2 (
    .J(AND_out), .clk(Clock_out), .K(AND_out), .Q(Q2), .Qn(JK2_qn), .preset(Preset), .en(Enable),
    .reset(Reset));
  and AND_2 (AND_2_out, JK2_qn, AND_out);
  J_K_Flip_Flop JK3 (
    .J(AND_2_out), .clk(Clock_out), .K(AND_2_out), .Q(Q3), .preset(Preset), .en(Enable), .reset(Reset));  // open: Qn
endmodule
