// Logisim project 4-bit synchronous UP counter.circ as structural Verilog: 1 circuit, main circuit main
module main (
  input  Enable,
  input  Preset,
  input  Reset,
  output Q0,
  output Q1,
  output Q2,
  output Q3
);

  wire AND_2_out, AND_out, Clock_out;

  Clock Clock (.out(Clock_out));
  J_K_Flip_Flop JK0 (
    .J(1'b1), .clk(Clock_out), .K(1'b1), .Q(Q0), .preset(Preset), .en(Enable), .reset(Reset));  // open: Qn
  J_K_Flip_Flop JK1 (.J(Q0), .clk(Clock_out), .K(Q0), .Q(Q1), .preset(Preset), .en(Enable), .reset(Reset));  // open: Qn
  and AND (AND_out, Q0, Q1);
  J_K_Flip_Flop JK2 (
    .J(AND_out), .clk(Clock_out), .K(AND_out), .Q(Q2), .preset(Preset), .en(Enable), .reset(Reset));  // open: Qn
  and AND_2 (AND_2_out, AND_out, Q2);
  J_K_Flip_Flop JK3 (
    .J(AND_2_out), .clk(Clock_out), .K(AND_2_out), .Q(Q3), .preset(Preset), .en(Enable), .reset(Reset));  // open: Qn
endmodule
