// Logisim project 4-bit_Up_Down_Counter.circ as structural Verilog: 1 circuit, main circuit main
module main (
  input  Up,
  input  Preset,
  input  Enable,
  input  Reset,
  output Q0,
  output Q1,
  output Q2,
  output Q3
);

  wire AND_2_out, AND_3_out, AND_4_out, AND_5_out, AND_6_out, AND_out, Clockl_out, JK0_qn, JK1_qn, JK2_qn,
       NOT_out, OR_2_out, OR_3_out, OR_out;

  not NOT (NOT_out, Up);
  Clock Clockl (.out(Clockl_out));
  J_K_Flip_Flop JK0 (
    .J(1'b1), .clk(Clockl_out), .K(1'b1), .Q(Q0), .Qn(JK0_qn), .preset(Preset), .en(Enable), .reset(Reset));
  and AND (AND_out, NOT_out, Q0);
  or OR (OR_out, AND_2_out, AND_out);
  and AND_2 (AND_2_out, JK0_qn, Up);
  J_K_Flip_Flop JK1 (
    .J(OR_out), .clk(Clockl_out), .K(OR_out), .Q(Q1), .Qn(JK1_qn), .preset(Preset), .en(Enable), .reset(Reset));
  and AND_3 (AND_3_out, Q1, AND_out, NOT_out);
  or OR_2 (OR_2_out, AND_4_out, AND_3_out);
  and AND_4 (AND_4_out, JK1_qn, AND_2_out, Up);
  J_K_Flip_Flop JK2 (
    .J(OR_2_out), .clk(Clockl_out), .K(OR_2_out), .Q(Q2), .Qn(JK2_qn), .preset(Preset), .en(Enable),
    .reset(Reset));
  and AND_5 (AND_5_out, AND_3_out, NOT_out, Q2);
  or OR_3 (OR_3_out, AND_6_out, AND_5_out);
  and AND_6 (AND_6_out, JK2_qn, AND_4_out, Up);
  J_K_Flip_Flop JK3 (
    .J(OR_3_out), .clk(Clockl_out), .K(OR_3_out), .Q(Q3), .preset(Preset), .en(Enable), .reset(Reset));  // open: Qn
endmodule
