// Logisim project 8x1 Multiplexer.circ as structural Verilog: 1 circuit, main circuit main
module main (
  input  S2,
  input  S1,
  input  S0,
  input  I0,
  input  I1,
  input  I2,
  input  I3,
  input  I4,
  input  I5,
  input  I6,
  input  I7,
  output Y
);

  wire AND0_out, AND1_out, AND2_out, AND3_out, AND4_out, AND5_out, AND6_out, AND7_out, not_1_out, not_2_out,
       not_3_out;

  not not_1 (not_1_out, S2);
  not not_2 (not_2_out, S1);
  not not_3 (not_3_out, S0);
  and AND0 (AND0_out, not_3_out, not_2_out, not_1_out, I0);
  and AND1 (AND1_out, S0, not_2_out, not_1_out, I1);
  and AND2 (AND2_out, not_3_out, S1, not_1_out, I2);
  and AND3 (AND3_out, S0, S1, not_1_out, I3);
  and AND4 (AND4_out, not_3_out, not_2_out, S2, I4);
  and AND5 (AND5_out, S0, not_2_out, not_1_out, I5);
  and AND6 (AND6_out, not_3_out, S1, S2, I6);
  and AND7 (AND7_out, S0, S1, S2, I7);
  or OR (Y, AND0_out, AND1_out, AND2_out, AND3_out, AND4_out, AND5_out, AND6_out, AND7_out);
endmodule
