// Logisim project ALU.circ as structural Verilog: 1 circuit, main circuit main
module main (
  input  A3,
  input  B3,
  input  A2,
  input  B2,
  input  A1,
  input  B1,
  input  A0,
  input  B0,
  input  Cin,
  input  [1:0] Select,
  input  EN,
  input  Select_2,
  input  EN_2,
  output Cout,
  output Q3,
  output Q2,
  output Q1,
  output Q0
);

  wire main_1_cout, main_1_s0, main_1_s1, main_1_s2, main_1_s3, main_2_s0, main_2_s1, main_2_s2, main_2_s3,
       NOT_out, pull_resistor_1_node;

  not NOT (NOT_out, EN);
  Arithmetic_circuit_main main_1 (
    .A3(A3), .B3(B3), .A2(A2), .B2(B2), .A1(A1), .B1(B1), .A0(A0), .B0(B0), .Cin(Cin), .Select(Select),
    .EN(NOT_out), .Cout(main_1_cout), .S3(main_1_s3), .S2(main_1_s2), .S1(main_1_s1), .S0(main_1_s0));
  Logic_circuit_main main_2 (
    .S3(main_2_s3), .S2(main_2_s2), .S1(main_2_s1), .S0(main_2_s0), .A3(A3), .B3(B3), .A2(A2), .B2(B2),
    .A1(A1), .B1(B1), .A0(A0), .B0(B0), .Select(Select), .EN(EN));
  Pull_Resistor pull_resistor_1 (.node(pull_resistor_1_node));
  Multiplexer multiplexer_1 (.in0(pull_resistor_1_node), .in1(main_1_cout), .out(Cout), .sel(Select_2), .en(EN_2));
  Multiplexer multiplexer_2 (.in0(main_1_s3), .in1(main_2_s3), .out(Q3), .sel(Select_2), .en(EN_2));
  Multiplexer multiplexer_3 (.in0(main_1_s2), .in1(main_2_s2), .out(Q2), .sel(Select_2), .en(EN_2));
  Multiplexer multiplexer_4 (.in0(main_1_s1), .in1(main_2_s1), .out(Q1), .sel(Select_2), .en(EN_2));
  Multiplexer multiplexer_5 (.in0(main_1_s0), .in1(main_2_s0), .out(Q0), .sel(Select_2), .en(EN_2));
endmodule
