// Logisim project Arithmetic circuit.circ as structural Verilog: 1 circuit, main circuit main
module main (
  input  A3,
  input  B3,
  input  A2,
  input  B2,
  input  A1,
  input  B1,
  input  A0,
  input  B0,
  input  [1:0] Select,
  input  EN,
  input  Cin,
  output Cout,
  output S3,
  output S2,
  output S1,
  output S0
);

  wire main_2_c, main_3_c, main_4_c, multiplexer_1_out, multiplexer_2_out, multiplexer_3_out,
       multiplexer_4_out, not_2_out, not_3_out, not_4_out, not_5_out, NOT_out, pull_resistor_1_node;

  not NOT (NOT_out, pull_resistor_1_node);
  Pull_Resistor #(.pull(1)) pull_resistor_1 (.node(pull_resistor_1_node));
  not not_2 (not_2_out, B3);
  not not_3 (not_3_out, B2);
  not not_4 (not_4_out, B1);
  not not_5 (not_5_out, B0);
  Multiplexer #(.select(2)) multiplexer_1 (
    .in0(B3), .in1(not_2_out), .in2(NOT_out), .in3(pull_resistor_1_node), .out(multiplexer_1_out),
    .sel(Select), .en(EN));
  Multiplexer #(.select(2)) multiplexer_2 (
    .in0(B2), .in1(not_3_out), .in2(NOT_out), .in3(pull_resistor_1_node), .out(multiplexer_2_out),
    .sel(Select), .en(EN));
  Multiplexer #(.select(2)) multiplexer_3 (
    .in0(B1), .in1(not_4_out), .in2(NOT_out), .in3(pull_resistor_1_node), .out(multiplexer_3_out),
    .sel(Select), .en(EN));
  Multiplexer #(.select(2)) multiplexer_4 (
    .in0(B0), .in1(not_5_out), .in2(NOT_out), .in3(pull_resistor_1_node), .out(multiplexer_4_out),
    .sel(Select), .en(EN));
  Full_Adder_using_half_adder_main main_1 (.A(A3), .B(multiplexer_1_out), .Cin(main_2_c), .S(S3), .C(Cout));
  Full_Adder_using_half_adder_main main_2 (.A(A2), .B(multiplexer_2_out), .Cin(main_3_c), .S(S2), .C(main_2_c));
  Full_Adder_using_half_adder_main main_3 (.A(A1), .B(multiplexer_3_out), .Cin(main_4_c), .S(S1), .C(main_3_c));
  Full_Adder_using_half_adder_main main_4 (.A(A0), .B(multiplexer_4_out), .Cin(Cin), .S(S0), .C(main_4_c));
endmodule
