// Logisim project Carry look ahead ADDER.circ as structural Verilog: 1 circuit, main circuit main
module main (
  input  A3,
  input  B3,
  input  A2,
  input  B2,
  input  A1,
  input  B1,
  input  A0,
  input  B0,
  input  Cin,
  output Cout,
  output S3,
  output S2,
  output S1,
  output S0
);

  wire and_1_out, and_2_out, and_3_out, and_4_out, CLG_c1, CLG_c2, CLG_c3, xor_1_out, xor_2_out, xor_3_out,
       xor_4_out;

  xor xor_1 (xor_1_out, A3, B3);
  and and_1 (and_1_out, B3, A3);
  xor xor_2 (xor_2_out, A2, B2);
  and and_2 (and_2_out, B2, A2);
  xor xor_3 (xor_3_out, A1, B1);
  and and_3 (and_3_out, B1, A1);
  xor xor_4 (xor_4_out, A0, B0);
  and and_4 (and_4_out, B0, A0);
  Carry_look_ahead_GENERATOR_main CLG (
    .G3(and_1_out), .P3(xor_1_out), .G2(and_2_out), .P2(xor_2_out), .G1(and_3_out), .P1(xor_3_out),
    .G0(and_4_out), .P0(xor_4_out), .Cin(Cin), .Cout(Cout), .C3(CLG_c3), .C2(CLG_c2), .C1(CLG_c1));
  xor xor_5 (S3, xor_1_out, CLG_c3);
  xor xor_6 (S2, xor_2_out, CLG_c2);
  xor xor_7 (S1, xor_3_out, CLG_c1);
  xor xor_8 (S0, xor_4_out, Cin);
endmodule
