// Logisim project CommonBus.circ as structural Verilog: 1 circuit, main circuit main
module main (
  input  Enable,
  input  [1:0] Select_Bit,
  input  SR0,
  input  PR,
  input  EN,
  input  CL,
  input  SR1,
  input  PR_2,
  input  EN_2,
  input  CL_2,
  input  SR2,
  input  PR_3,
  input  EN_3,
  input  CL_3,
  input  SR3,
  input  PR_4,
  input  EN_4,
  input  CL_4,
  output D0,
  output D1,
  output D2,
  output D3
);

  wire Clock_out, R0_p0, R0_p1, R0_p2, R0_serialout, R1_p0, R1_p1, R1_p2, R1_serialout, R2_p0, R2_p1, R2_p2,
       R2_serialout, R3_p0, R3_p1, R3_p2, R3_serialout;

  Clock Clock (.out(Clock_out));
  Multiplexer #(.select(2)) multiplexer_1 (
    .in0(R0_p0), .in1(R1_p0), .in2(R2_p0), .in3(R3_p0), .out(D0), .sel(Select_Bit), .en(Enable));
  SIPO_main R0 (
    .Serial_In(SR0), .CLK(Clock_out), .Preset(PR), .Reset(CL), .P0(R0_p0), .P1(R0_p1), .P2(R0_p2),
    .SerialOut(R0_serialout), .Enable(EN));
  Multiplexer #(.select(2)) multiplexer_2 (
    .in0(R0_p1), .in1(R1_p1), .in2(R2_p1), .in3(R3_p1), .out(D1), .sel(Select_Bit), .en(Enable));
  SIPO_main R1 (
    .Serial_In(SR1), .CLK(Clock_out), .Preset(PR_2), .Reset(CL_2), .P0(R1_p0), .P1(R1_p1), .P2(R1_p2),
    .SerialOut(R1_serialout), .Enable(EN_2));
  SIPO_main R2 (
    .Serial_In(SR2), .CLK(Clock_out), .Preset(PR_3), .Reset(CL_3), .P0(R2_p0), .P1(R2_p1), .P2(R2_p2),
    .SerialOut(R2_serialout), .Enable(EN_3));
  Multiplexer #(.select(2)) multiplexer_3 (
    .in0(R0_p2), .in1(R1_p2), .in2(R2_p2), .in3(R3_p2), .out(D2), .sel(Select_Bit), .en(Enable));
  Multiplexer #(.select(2)) multiplexer_4 (
    .in0(R0_serialout), .in1(R1_serialout), .in2(R2_serialout), .in3(R3_serialout), .out(D3),
    .sel(Select_Bit), .en(Enable));
  SIPO_main R3 (
    .Serial_In(SR3), .CLK(Clock_out), .Preset(PR_4), .Reset(CL_4), .P0(R3_p0), .P1(R3_p1), .P2(R3_p2),
    .SerialOut(R3_serialout), .Enable(EN_4));
endmodule
