// Logisim project D-Flip Flop.circ as structural Verilog: 1 circuit, main circuit main
module main (
  input  Din,
  output Dout
);

  wire AND_2_out, AND_out, Clock_out, NOT_out;

  not NOT (NOT_out, Din);
  Clock Clock (.out(Clock_out));
  and AND (AND_out, Din, Clock_out);
  and AND_2 (AND_2_out, Clock_out, NOT_out);
  S_R_Latch_main main_1 (.S(AND_out), .R(AND_2_out), .Q(Dout));  // open: Qcomp
endmodule
