// Logisim project Full Adder using half adder.circ as structural Verilog: 1 circuit, main circuit main
module main (
  input  A,
  input  B,
  input  Cin,
  output S,
  output C
);

  wire main_1_c, main_1_s, main_2_c;

  Half_Adder_main main_1 (.A(A), .in_2(B), .S(main_1_s), .C(main_1_c));
  Half_Adder_main main_2 (.A(main_1_s), .in_2(Cin), .S(S), .C(main_2_c));
  or OR (C, main_2_c, main_1_c);

  // Notes on the sheet:
  //   HA1
  //   FULL ADDER
  //   HA2
endmodule
