// Logisim project Full Subtractor Using Gates.circ as structural Verilog: 1 circuit, main circuit main
module main (
  input  A,
  input  B,
  input  Bin,
  output D,
  output Bout
);

  wire AND1_out, AND2_out, AND3_out, not_1_out;

  not not_1 (not_1_out, A);
  and AND1 (AND1_out, not_1_out, Bin);
  and AND2 (AND2_out, not_1_out, B);
  and AND3 (AND3_out, B, Bin);
  xor XOR (D, A, B, Bin);
  or OR (Bout, AND1_out, AND2_out, AND3_out);
endmodule
