// Logisim project Full Subtractor using half subtractor.circ as structural Verilog: 1 circuit, main circuit main
module main (
  input  A,
  input  B,
  input  Bin,
  output D,
  output Bout
);

  wire HS1_b, HS1_d, HS2_b;

  Half_Subtractor_main HS1 (.in_1(A), .in_2(B), .D(HS1_d), .B(HS1_b));
  Half_Subtractor_main HS2 (.in_1(HS1_d), .in_2(Bin), .D(D), .B(HS2_b));
  or OR (Bout, HS2_b, HS1_b);
endmodule
