// Logisim project Half Adder.circ as structural Verilog: 1 circuit, main circuit main
module main (
  input  A,
  input  in_2,
  output S,
  output C
);

  xor XOR1 (S, A, in_2);
  and AND1 (C, A, in_2);

  // Notes on the sheet:
  //   HALF ADDER
endmodule
