// Logisim project Half Subtractor.circ as structural Verilog: 1 circuit, main circuit main
module main (
  input  in_1,
  input  in_2,
  output D,
  output B
);

  wire not_1_out;

  not not_1 (not_1_out, in_1);
  xor XOR1 (D, in_1, in_2);
  and AND1 (B, not_1_out, in_2);

  // Notes on the sheet:
  //   HALF SUBTRACTOR
endmodule
