// Logisim project Logic circuit.circ as structural Verilog: 1 circuit, main circuit main
module main (
  input  A3,
  input  B3,
  input  A2,
  input  B2,
  input  A1,
  input  B1,
  input  A0,
  input  B0,
  input  [1:0] Select,
  input  EN,
  output S3,
  output S2,
  output S1,
  output S0
);

  wire AND_2_out, AND_3_out, AND_4_out, AND_out, NOT_2_out, NOT_3_out, NOT_4_out, NOT_out, OR_2_out,
       OR_3_out, OR_4_out, OR_out, XOR_2_out, XOR_3_out, XOR_4_out, XOR_out;

  and AND (AND_out, A3, B3);
  or OR (OR_out, A3, B3);
  not NOT (NOT_out, A3);
  and AND_2 (AND_2_out, A2, B2);
  or OR_2 (OR_2_out, A2, B2);
  not NOT_2 (NOT_2_out, A2);
  and AND_3 (AND_3_out, A1, B1);
  or OR_3 (OR_3_out, A1, B1);
  not NOT_3 (NOT_3_out, A1);
  and AND_4 (AND_4_out, A0, B0);
  or OR_4 (OR_4_out, A0, B0);
  not NOT_4 (NOT_4_out, A0);
  xor XOR (XOR_out, A3, B3);
  xor XOR_2 (XOR_2_out, A2, B2);
  xor XOR_3 (XOR_3_out, A1, B1);
  xor XOR_4 (XOR_4_out, A0, B0);
  Multiplexer #(.select(2)) multiplexer_1 (
    .in0(AND_out), .in1(OR_out), .in2(NOT_out), .in3(XOR_out), .out(S3), .sel(Select), .en(EN));
  Multiplexer #(.select(2)) multiplexer_2 (
    .in0(AND_2_out), .in1(OR_2_out), .in2(NOT_2_out), .in3(XOR_2_out), .out(S2), .sel(Select), .en(EN));
  Multiplexer #(.select(2)) multiplexer_3 (
    .in0(AND_3_out), .in1(OR_3_out), .in2(NOT_3_out), .in3(XOR_3_out), .out(S1), .sel(Select), .en(EN));
  Multiplexer #(.select(2)) multiplexer_4 (
    .in0(AND_4_out), .in1(OR_4_out), .in2(NOT_4_out), .in3(XOR_4_out), .out(S0), .sel(Select), .en(EN));
endmodule
