// Logisim project Memory 1 bit.circ as structural Verilog: 1 circuit, main circuit main
module main (
  input  Din,
  input  Clock,
  input  Enable,
  input  Read_1__Write_0,
  output Dout
);

  wire AND_2_out, AND_out, main_1_q, NOT_2_out, NOT_out;

  not NOT (NOT_out, Din);
  and AND (AND_out, Din, NOT_2_out, Enable, Clock);
  and AND_2 (AND_2_out, Clock, Enable, NOT_2_out, NOT_out);
  not NOT_2 (NOT_2_out, Read_1__Write_0);
  S_R_Latch_main main_1 (.S(AND_out), .R(AND_2_out), .Q(main_1_q));  // open: Qcomp
  and AND_3 (Dout, main_1_q, Enable, Read_1__Write_0);
endmodule
