// Logisim project Memory 16bit.circ as structural Verilog: 1 circuit, main circuit main
module main (
  input  D0,
  input  D1,
  input  D2,
  input  D3,
  input  Read_Write,
  input  A,
  input  B,
  input  S,
  output Dout_0,
  output Dout_1,
  output Dout_2,
  output Dout_3
);

  wire Clock_out, main_1_a0, main_1_a1, main_1_a2, main_1_a3, main_2_dout, main_3_dout, main_4_dout,
       main_5_dout, main_6_dout, main_7_dout, main_8_dout, main_9_dout, main_10_dout, main_11_dout,
       main_12_dout, main_13_dout, main_14_dout, main_15_dout, main_16_dout, main_17_dout;

  _2X4_Decoder_main main_1 (.A0(main_1_a0), .A1(main_1_a1), .A2(main_1_a2), .A3(main_1_a3), .A(A), .B(B), .E(S));
  Clock Clock (.out(Clock_out));
  Memory_1_bit_main main_2 (
    .Din(D0), .Clock(Clock_out), .Enable(main_1_a0), .Dout(main_2_dout), .Read_1__Write_0(Read_Write));
  Memory_1_bit_main main_3 (
    .Din(D0), .Clock(Clock_out), .Enable(main_1_a1), .Dout(main_3_dout), .Read_1__Write_0(Read_Write));
  Memory_1_bit_main main_4 (
    .Din(D0), .Clock(Clock_out), .Enable(main_1_a2), .Dout(main_4_dout), .Read_1__Write_0(Read_Write));
  Memory_1_bit_main main_5 (
    .Din(D0), .Clock(Clock_out), .Enable(main_1_a3), .Dout(main_5_dout), .Read_1__Write_0(Read_Write));
  or OR1 (Dout_0, main_5_dout, main_4_dout, main_3_dout, main_2_dout);
  Memory_1_bit_main main_6 (
    .Din(D1), .Clock(Clock_out), .Enable(main_1_a0), .Dout(main_6_dout), .Read_1__Write_0(Read_Write));
  Memory_1_bit_main main_7 (
    .Din(D1), .Clock(Clock_out), .Enable(main_1_a1), .Dout(main_7_dout), .Read_1__Write_0(Read_Write));
  Memory_1_bit_main main_8 (
    .Din(D1), .Clock(Clock_out), .Enable(main_1_a2), .Dout(main_8_dout), .Read_1__Write_0(Read_Write));
  Memory_1_bit_main main_9 (
    .Din(D1), .Clock(Clock_out), .Enable(main_1_a3), .Dout(main_9_dout), .Read_1__Write_0(Read_Write));
  or OR2 (Dout_1, main_9_dout, main_8_dout, main_7_dout, main_6_dout);
  Memory_1_bit_main main_10 (
    .Din(D2), .Clock(Clock_out), .Enable(main_1_a0), .Dout(main_10_dout), .Read_1__Write_0(Read_Write));
  Memory_1_bit_main main_11 (
    .Din(D2), .Clock(Clock_out), .Enable(main_1_a1), .Dout(main_11_dout), .Read_1__Write_0(Read_Write));
  Memory_1_bit_main main_12 (
    .Din(D2), .Clock(Clock_out), .Enable(main_1_a2), .Dout(main_12_dout), .Read_1__Write_0(Read_Write));
  Memory_1_bit_main main_13 (
    .Din(D2), .Clock(Clock_out), .Enable(main_1_a3), .Dout(main_13_dout), .Read_1__Write_0(Read_Write));
  or OR3 (Dout_2, main_13_dout, main_12_dout, main_11_dout, main_10_dout);
  Memory_1_bit_main main_14 (
    .Din(D3), .Clock(Clock_out), .Enable(main_1_a0), .Dout(main_14_dout), .Read_1__Write_0(Read_Write));
  Memory_1_bit_main main_15 (
    .Din(D3), .Clock(Clock_out), .Enable(main_1_a1), .Dout(main_15_dout), .Read_1__Write_0(Read_Write));
  Memory_1_bit_main main_16 (
    .Din(D3), .Clock(Clock_out), .Enable(main_1_a2), .Dout(main_16_dout), .Read_1__Write_0(Read_Write));
  Memory_1_bit_main main_17 (
    .Din(D3), .Clock(Clock_out), .Enable(main_1_a3), .Dout(main_17_dout), .Read_1__Write_0(Read_Write));
  or OR4 (Dout_3, main_17_dout, main_16_dout, main_15_dout, main_14_dout);
endmodule
