// Logisim project PISO.circ as structural Verilog: 1 circuit, main circuit main
module main (
  input  Load_Shift,
  input  D0,
  input  D1,
  input  D2,
  input  D3,
  input  Preset,
  input  Enable,
  input  Clear,
  output Serial_Out
);

  wire AND_2_out, AND_3_out, AND_4_out, AND_5_out, AND_6_out, AND_7_out, AND_out, Clock_out, JK0_q, JK1_q,
       JK2_q, NOT_2_out, NOT_3_out, NOT_4_out, NOT_5_out, NOT_out, OR_2_out, OR_3_out, OR_out;

  not NOT (NOT_out, Load_Shift);
  and AND (AND_out, Load_Shift, D0);
  not NOT_2 (NOT_2_out, AND_out);
  Clock Clock (.out(Clock_out));
  and AND_2 (AND_2_out, JK0_q, NOT_out);
  J_K_Flip_Flop JK0 (
    .J(AND_out), .clk(Clock_out), .K(NOT_2_out), .Q(JK0_q), .preset(Preset), .en(Enable), .reset(Clear));  // open: Qn
  not NOT_3 (NOT_3_out, OR_out);
  and AND_3 (AND_3_out, Load_Shift, D1);
  or OR (OR_out, AND_2_out, AND_3_out);
  J_K_Flip_Flop JK1 (
    .J(OR_out), .clk(Clock_out), .K(NOT_3_out), .Q(JK1_q), .preset(Preset), .en(Enable), .reset(Clear));  // open: Qn
  and AND_4 (AND_4_out, Load_Shift, D2);
  and AND_5 (AND_5_out, JK1_q, NOT_out);
  or OR_2 (OR_2_out, AND_5_out, AND_4_out);
  not NOT_4 (NOT_4_out, OR_2_out);
  and AND_6 (AND_6_out, Load_Shift, D3);
  and AND_7 (AND_7_out, JK2_q, NOT_out);
  or OR_3 (OR_3_out, AND_7_out, AND_6_out);
  J_K_Flip_Flop JK2 (
    .J(OR_2_out), .clk(Clock_out), .K(NOT_4_out), .Q(JK2_q), .preset(Preset), .en(Enable), .reset(Clear));  // open: Qn
  not NOT_5 (NOT_5_out, OR_3_out);
  J_K_Flip_Flop JK3 (
    .J(OR_3_out), .clk(Clock_out), .K(NOT_5_out), .Q(Serial_Out), .preset(Preset), .en(Enable), .reset(Clear));  // open: Qn
endmodule
