// Logisim project Ripple Carry Full Adder (Half Adder).circ as structural Verilog: 1 circuit, main circuit main
module main (
  input  B0,
  input  B1,
  input  B2,
  input  B3,
  input  A0,
  input  A1,
  input  A2,
  input  A3,
  input  Cin,
  output Cout,
  output S0,
  output S1,
  output S2,
  output S3
);

  wire FA0_c, FA1_c, FA2_c;

  Full_Adder_using_half_adder_main FA0 (.A(A0), .B(B0), .Cin(Cin), .S(S0), .C(FA0_c));
  Full_Adder_using_half_adder_main FA1 (.A(A1), .B(B1), .Cin(FA0_c), .S(S1), .C(FA1_c));
  Full_Adder_using_half_adder_main FA2 (.A(A2), .B(B2), .Cin(FA1_c), .S(S2), .C(FA2_c));
  Full_Adder_using_half_adder_main FA3 (.A(A3), .B(B3), .Cin(FA2_c), .S(S3), .C(Cout));

  // Notes on the sheet:
  //   4 BIT RIPPLE CARRY FULL ADDER
endmodule
