// Logisim project Ripple Carry Full Adder.circ as structural Verilog: 1 circuit, main circuit main
module main (
  input  B0,
  input  A0,
  input  B1,
  input  A1,
  input  B2,
  input  A2,
  input  B3,
  input  A3,
  input  Cin,
  output Cout,
  output S0,
  output S1,
  output S2,
  output S3
);

  wire FA0_p3, FA1_p3, FA2_p3;

  // Full_Adder_main FA0: pin names not known; wires that end beside it: Cin, S0, FA0_p3
  // Full_Adder_main FA1: pin names not known; wires that end beside it: FA0_p3, S1, FA1_p3
  // Full_Adder_main FA2: pin names not known; wires that end beside it: FA1_p3, S2, FA2_p3
  // Full_Adder_main FA3: pin names not known; wires that end beside it: FA2_p3, S3, Cout

  // Notes on the sheet:
  //   4 BIT RIPPLE CARRY FULL ADDER 
endmodule
