// Logisim project S-R Latch.circ as structural Verilog: 1 circuit, main circuit main
module main (
  input  S,
  input  R,
  output Qcomp,
  output Q
);

  nor NOR (Qcomp, S, Q);
  nor NOR_2 (Q, Qcomp, R);
endmodule
