// Logisim project SIPO.circ as structural Verilog: 1 circuit, main circuit main
module main (
  input  Serial_In,
  input  CLK,
  input  Preset,
  input  Enable,
  input  Reset,
  output P0,
  output P1,
  output P2,
  output SerialOut
);

  wire JK0_qn, JK1_qn, JK2_qn, not_1_out;

  not not_1 (not_1_out, Serial_In);
  J_K_Flip_Flop JK0 (
    .J(Serial_In), .clk(CLK), .K(not_1_out), .Q(P0), .Qn(JK0_qn), .preset(Preset), .en(Enable), .reset(Reset));
  J_K_Flip_Flop JK1 (.J(P0), .clk(CLK), .K(JK0_qn), .Q(P1), .Qn(JK1_qn), .preset(Preset), .en(Enable), .reset(Reset));
  J_K_Flip_Flop JK2 (.J(P1), .clk(CLK), .K(JK1_qn), .Q(P2), .Qn(JK2_qn), .preset(Preset), .en(Enable), .reset(Reset));
  J_K_Flip_Flop JK3 (
    .J(P2), .clk(CLK), .K(JK2_qn), .Q(SerialOut), .preset(Preset), .en(Enable), .reset(Reset));  // open: Qn
endmodule
