// Logisim project SISO.circ as structural Verilog: 1 circuit, main circuit main
module main (
  input  Serial_In,
  input  Clock,
  input  Preset,
  input  Enable,
  input  Clear,
  output D3
);

  wire JK0_q, JK0_qn, JK1_q, JK1_qn, JK2_q, JK2_qn, NOT_out;

  not NOT (NOT_out, Serial_In);
  J_K_Flip_Flop JK0 (
    .J(Serial_In), .clk(Clock), .K(NOT_out), .Q(JK0_q), .Qn(JK0_qn), .preset(Preset), .en(Enable),
    .reset(Clear));
  J_K_Flip_Flop JK1 (
    .J(JK0_q), .clk(Clock), .K(JK0_qn), .Q(JK1_q), .Qn(JK1_qn), .preset(Preset), .en(Enable), .reset(Clear));
  J_K_Flip_Flop JK2 (
    .J(JK1_q), .clk(Clock), .K(JK1_qn), .Q(JK2_q), .Qn(JK2_qn), .preset(Preset), .en(Enable), .reset(Clear));
  J_K_Flip_Flop JK3 (
    .J(JK2_q), .clk(Clock), .K(JK2_qn), .Q(D3), .preset(Preset), .en(Enable), .reset(Clear));  // open: Qn

  // Notes on the sheet:
  //   Serial Out
endmodule
