// Logisim project Full Adder.circ as structural Verilog: 1 circuit, main circuit Full Adder 
// FA
module Full_Adder (
  input  A,
  input  B,
  input  C,
  output Sum,
  output Carry
);

  wire half_adder_1_c, half_adder_1_s, half_adder_2_c;

  Half_Adder half_adder_1 (.A(A), .B(B), .S(half_adder_1_s), .C(half_adder_1_c));
  Half_Adder half_adder_2 (.A(half_adder_1_s), .B(C), .S(Sum), .C(half_adder_2_c));
  or or_1 (Carry, half_adder_2_c, half_adder_1_c);
endmodule
