// Logisim project Half Adder.circ as structural Verilog: 1 circuit, main circuit Half Adder
module Half_Adder (
  input  A,
  input  B,
  output S,
  output C
);

  xor XOR (S, A, B);
  and AND (C, A, B);
endmodule
