// Logisim project Ripple Carry.circ as structural Verilog: 1 circuit, main circuit Ripple carry
module Ripple_carry (
  input  A0,
  input  B0,
  input  A1,
  input  B1,
  input  A2,
  input  B2,
  input  A3,
  input  B3,
  input  Carry_in,
  output Carry_out,
  output S0,
  output S1,
  output S2,
  output S3
);

  wire full_adder_1_carry, full_adder_2_carry, full_adder_3_carry;

  Full_Adder full_adder_1 (.A(A0), .B(B0), .C(Carry_in), .Sum(S0), .Carry(full_adder_1_carry));
  Full_Adder full_adder_2 (.A(A1), .B(B1), .C(full_adder_1_carry), .Sum(S1), .Carry(full_adder_2_carry));
  Full_Adder full_adder_3 (.A(A2), .B(B2), .C(full_adder_2_carry), .Sum(S2), .Carry(full_adder_3_carry));
  Full_Adder full_adder_4 (.A(A3), .B(B3), .C(full_adder_3_carry), .Sum(S3), .Carry(Carry_out));
endmodule
