// Logisim project Wallace tree adder(3 numbers).circ as structural Verilog: 1 circuit, main circuit main
module main (
  input  A0,
  input  B0,
  input  C0,
  input  A1,
  input  B1,
  input  C1,
  input  A2,
  input  B2,
  input  C2,
  input  A3,
  input  B3,
  input  C3,
  output S0,
  output S1,
  output S2,
  output S3,
  output S4,
  output Cout
);

  wire full_adder_1_carry, full_adder_2_carry, full_adder_2_sum, full_adder_3_carry, full_adder_3_sum,
       full_adder_4_carry, full_adder_4_sum;

  Full_Adder full_adder_1 (.A(B0), .B(C0), .C(A0), .Sum(S0), .Carry(full_adder_1_carry));
  Full_Adder full_adder_2 (.A(B1), .B(C1), .C(A1), .Sum(full_adder_2_sum), .Carry(full_adder_2_carry));
  Full_Adder full_adder_3 (.A(B2), .B(C2), .C(A2), .Sum(full_adder_3_sum), .Carry(full_adder_3_carry));
  Ripple_carry ripple_carry_1 (
    .Carry_in(1'b0), .A0(full_adder_1_carry), .B0(full_adder_2_sum), .A1(full_adder_2_carry),
    .B1(full_adder_3_sum), .A2(full_adder_3_carry), .B2(full_adder_4_sum), .A3(full_adder_4_carry),
    .B3(1'b0), .S0(S1), .S1(S2), .S2(S3), .S3(S4), .Carry_out(Cout));
  Full_Adder full_adder_4 (.A(B3), .B(C3), .C(A3), .Sum(full_adder_4_sum), .Carry(full_adder_4_carry));
endmodule
