// Logisim project Wallace tree adder(7-bit).circ as structural Verilog: 1 circuit, main circuit main
module main (
  input  G,
  input  A,
  input  B,
  input  C,
  input  D,
  input  E,
  input  F,
  output S0,
  output S1,
  output Cout
);

  wire full_adder_1_carry, full_adder_1_sum, full_adder_2_carry, full_adder_2_sum, full_adder_3_carry;

  Full_Adder full_adder_1 (.A(B), .B(A), .C(C), .Sum(full_adder_1_sum), .Carry(full_adder_1_carry));
  Full_Adder full_adder_2 (.A(E), .B(D), .C(F), .Sum(full_adder_2_sum), .Carry(full_adder_2_carry));
  Full_Adder full_adder_3 (.A(G), .B(full_adder_2_sum), .C(full_adder_1_sum), .Sum(S0), .Carry(full_adder_3_carry));
  Full_Adder full_adder_4 (
    .A(full_adder_1_carry), .B(full_adder_3_carry), .C(full_adder_2_carry), .Sum(S1), .Carry(Cout));
endmodule
